# Fritzing sketch fire (saved by Fritzing 0.9.0b)

parts:
  Part1 = Arduino Pro Mini v13
  NEOPIXEL1 = Neopixel Strip -- Black (30/m)
  C1 = Electrolytic Capacitor [capacitance=1µF package="100 mil [THT, electrolytic]"]
  IR1 = TSOP312.., 314.. [package=THT]
  S1 = Momentary Switch [package=tactile-pth]
  R3 = Resistor [tolerance=±5% resistance=330 package="0603 [SMD]"]
  R2 = Resistor [tolerance=±5% resistance=15k package="0603 [SMD]"]
  R1 = Resistor [tolerance=±5% resistance=220k package="0603 [SMD]"]
  JACK1 = 2.1mm Barrel Jack with Terminal Block

nets:
  GND: Part1.GND, NEOPIXEL1.GND, C1.-, IR1.Vs, S1.1, R1.Pin_1, JACK1.NEG
  N1: Part1.VCC, NEOPIXEL1.DI, C1.+, IR1.Data, R2.Pin_1, JACK1.POS
  N2: Part1.D5_PWM, IR1.GND
  N3: Part1.D4, R3.Pin_1
  N4: Part1.D2, S1.2, R2.Pin_0, R1.Pin_0
  N5: NEOPIXEL1.+5V, R3.Pin_0

custom parts:
  Neopixel Strip -- Black (30/m): Neopixel Strip, Black, 30 pixels per meter.
